# Fritzing sketch Kiln-Controller2 (saved by Fritzing 1.0.6)
circuit board: 6.44777cm x 5.61225cm
breadboards: 1

parts:
  MAX31856 = Adafruit MAX31856 Thermocouple Amp [part_number="Adafruit #3263"]
  1k = Resistor [tolerance=±5% resistance=1k power=0.25W package=THT]
  1k_2 = Resistor [tolerance=±5% resistance=1k power=0.25W package=THT]
  1k_3 = Resistor [tolerance=±5% resistance=1k power=0.25W package=THT]
  1k_4 = Resistor [tolerance=±5% resistance=1k power=0.25W package=THT]
  Raspberry_Pi1 = Raspberry Pi 2
  +_5v_- = Screw terminal - 2 pins [package=THT]
  +Relay- = screw terminal, 2 pins
  MAX31855 = Adafruit Thermocouple Amplifier MAX31855 [part_number="Adafruit #269"]
  BC547 = NPN-Transistor [package="TO92 [THT]"]

nets:
  N1: MAX31856.!CS, 1k_4.Pin_0, MAX31855.CS
  N2: MAX31856.SDO, 1k_3.Pin_0, MAX31855.DO
  N3: MAX31856.SCK, 1k_2.Pin_0, MAX31855.CLK
  GND: MAX31856.GND, Raspberry_Pi1.GND, +_5v_-.pin2, MAX31855.GND, BC547.E
  VIN: MAX31856.VIN, Raspberry_Pi1.5V, +_5v_-.pin1, +Relay-.pin1, MAX31855.VIN
  N4: 1k.Pin_0, BC547.B
  N5: 1k.Pin_1, Raspberry_Pi1.GPIO26
  N6: 1k_2.Pin_1, Raspberry_Pi1.GPIO22
  N7: 1k_3.Pin_1, Raspberry_Pi1.GPIO17
  N8: 1k_4.Pin_1, Raspberry_Pi1.GPIO27
  N9: +Relay-.pin2, BC547.C

custom parts:
  Adafruit MAX31856 Thermocouple Amp: Thermocouples are very sensitive, requiring a good amplifier with a cold-compensation reference, as well as calculations to handle any non-linearities. For a long time we've suggested our MAX31855K breakout, which works great but is only for K-type thermocouples. Now we're happy to offer a great new thermocouple amplifier/converter that can handle just about any type of thermocouple, and even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
  Adafruit Thermocouple Amplifier MAX31855: Thermocouples are very sensitive, requiring a good amplifier with a cold-compensation reference. The MAX31855K does everything for you, and can be easily interfaced with any microcontroller, even one without an analog input. This breakout board has the chip itself, a 3.3V regulator with 10uF bypass capacitors and level shifting circuitry, all assembled and tested. Comes with a 2 pin terminal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
